// Logisim project F5.circ as structural Verilog: 1 circuit, main circuit main
module main (
);

  wire and_1_out, and_2_out, CLK_out, comparator_1_eq, decoder_1_out0, decoder_1_out1, decoder_1_out2,
       decoder_1_out3, nand_1_out, not_1_out;
  wire [3:0] adder_1_out, multiplexer_1_out, PC_q, rom_1_data_2;
  wire [7:0] adder_2_out, bit_extender_1_out, multiplexer_2_out, multiplexer_3_out, multiplexer_4_out, R0_q,
       R1_Sum_q, R2_Cnt_q, R3_Cst_q, rom_1_data;

  Clock CLK (.out(CLK_out));
  Register #(.width(4)) PC (.D(multiplexer_1_out), .clk(CLK_out), .Q(PC_q));  // open: en, clr
  Multiplexer #(.width(4)) multiplexer_1 (
    .in0(adder_1_out), .in1(rom_1_data_2), .out(multiplexer_1_out), .sel(and_2_out));
  Adder #(.width(4)) adder_1 (.a(PC_q), .b(4'b0001), .out(adder_1_out));  // open: cin, cout
  ROM #(.addrWidth(4)) rom_1 (.addr(PC_q), .data({rom_1_data[7:6], rom_1_data_2, rom_1_data[1:0]}));
  and and_1 (and_1_out, rom_1_data[6], rom_1_data[7]);
  Decoder #(.select(2)) decoder_1 (
    .out0(decoder_1_out0), .out1(decoder_1_out1), .out2(decoder_1_out2), .out3(decoder_1_out3),
    .sel(rom_1_data_2[3:2]), .en(nand_1_out));
  nand nand_1 (nand_1_out, rom_1_data[6], rom_1_data[7]);
  assign bit_extender_1_out = {{4{1'b0}}, {rom_1_data_2[1:0], rom_1_data[1:0]}};  // Bit_Extender bit_extender_1
  Register R0 (.D(multiplexer_4_out), .en(decoder_1_out0), .clk(CLK_out), .Q(R0_q));  // open: clr
  Register R1_Sum (.D(multiplexer_4_out), .en(decoder_1_out1), .clk(CLK_out), .Q(R1_Sum_q));  // open: clr
  Register R2_Cnt (.D(multiplexer_4_out), .en(decoder_1_out2), .clk(CLK_out), .Q(R2_Cnt_q));  // open: clr
  Register R3_Cst (.D(multiplexer_4_out), .en(decoder_1_out3), .clk(CLK_out), .Q(R3_Cst_q));  // open: clr
  Multiplexer #(.select(2), .width(8)) multiplexer_2 (
    .in0(R0_q), .in1(R1_Sum_q), .in2(R2_Cnt_q), .in3(R3_Cst_q), .out(multiplexer_2_out),
    .sel(rom_1_data_2[1:0]));
  Multiplexer #(.select(2), .width(8)) multiplexer_3 (
    .in0(R0_q), .in1(R1_Sum_q), .in2(R2_Cnt_q), .in3(R3_Cst_q), .out(multiplexer_3_out), .sel(rom_1_data[1:0]));
  Adder adder_2 (.a(multiplexer_2_out), .b(multiplexer_3_out), .out(adder_2_out));  // open: cin, cout
  Comparator comparator_1 (.a(multiplexer_2_out), .b(multiplexer_3_out), .eq(comparator_1_eq));  // open: gt, lt
  not not_1 (not_1_out, comparator_1_eq);
  and and_2 (and_2_out, not_1_out, and_1_out);
  Multiplexer #(.select(2), .width(8)) multiplexer_4 (
    .in0(adder_2_out), .in2(bit_extender_1_out), .out(multiplexer_4_out), .sel(rom_1_data[7:6]));  // open: in1, in3

  // Notes on the sheet:
  //   contents of rom_1 (hex, n*v repeats v):
  //   8b 90 a1 b1 16 2b d2 dd
endmodule
