// Logisim project F6.circ as structural Verilog: 8 circuits, main circuit main
module main (
  input  EN,
  input  rst
);

  wire clk_out, controller_1_pcselect, controller_1_rmen, controller_1_wmen, controller_1_wordls,
       controller_1_wren, memory_1_byte0en, memory_1_byte1en, memory_1_byte2en, memory_1_byte3en;
  wire [1:0] controller_1_aluselect;
  wire [2:0] controller_1_insttype;
  wire [23:0] pc_1_pc_out;
  wire [31:0] alu_1_c, immediate_1_imm, memory_1_adressword, memory_1_dataout, memory_1_writeout, ram_1_dout,
       registers_1_p4, registers_1_p8, registers_1_p9, registers_1_p10, rom_1_data;
  wire [31:24] pc_1_pc_out_2;

  Clock clk (.out(clk_out));
  ROM #(.addrWidth(24), .dataWidth(32)) rom_1 (.addr(pc_1_pc_out), .data(rom_1_data));
  PC pc_1 (
    .PC_in(alu_1_c), .PC_select(controller_1_pcselect), .EN(EN), .clk(clk_out), .rst(rst),
    .PC_out({pc_1_pc_out_2, pc_1_pc_out}));
  Memory memory_1 (
    .wordLS(controller_1_wordls), .adress(alu_1_c), .dataIn(registers_1_p9), .readIn(ram_1_dout),
    .byte3EN(memory_1_byte3en), .byte2EN(memory_1_byte2en), .byte1EN(memory_1_byte1en),
    .byte0EN(memory_1_byte0en), .adressWord(memory_1_adressword), .writeOut(memory_1_writeout),
    .dataOut(memory_1_dataout));
  Controller controller_1 (
    .opcode(rom_1_data[6:0]), .funct3(rom_1_data[14:12]), .funct7(rom_1_data[31:25]),
    .ALUSelect(controller_1_aluselect), .pcSelect(controller_1_pcselect), .instType(controller_1_insttype),
    .wREN(controller_1_wren), .wMEN(controller_1_wmen), .rMEN(controller_1_rmen), .wordLS(controller_1_wordls));
  RAM #(.asyncread("true"), .byteenables("byteEnables"), .dataWidth(32), .\type ("nonvolatile")) ram_1 (
    .addr(memory_1_adressword[7:0]), .we(controller_1_wmen), .oe(controller_1_rmen), .clk(clk_out),
    .din(memory_1_writeout), .dout(ram_1_dout), .be3(memory_1_byte3en), .be2(memory_1_byte2en),
    .be1(memory_1_byte1en), .be0(memory_1_byte0en));
  Immediate immediate_1 (.instType(controller_1_insttype), .instruction(rom_1_data), .imm(immediate_1_imm));
  // Registers registers_1: pin names not known; wires that end beside it: clk_out, rst, rom_1_data[10:7], registers_1_p4, controller_1_wren, rom_1_data[18:15], rom_1_data[23:20], registers_1_p8, registers_1_p9, registers_1_p10
  Multiplexer #(.width(32)) multiplexer_1 (
    .in0(alu_1_c), .in1(memory_1_dataout), .out(registers_1_p4), .sel(controller_1_rmen));
  ALU alu_1 (
    .ALUSelect(controller_1_aluselect), .A(registers_1_p8), .imm(immediate_1_imm), .B(registers_1_p10),
    .C(alu_1_c));

  // Notes on the sheet:
  //   add, addi, lui, lw, lbu, sw, sb, jalr
  //   contents of rom_1 (hex, n*v repeats v):
  //   413 51137 10113 22c00093 80e7 fea12823 fe812e23 40800413 ff014183 3401b3 1c183 ff114203 440233 24203
  //   4181b3 ff214203 440233 24203 4181b3 ff314203 440233 24203 4181b3 40000213 320233 24203 ffc12403
  //   420233 420233 410233 9400193 fe312823 9000193 fe312623 fec22203 20067 8067 ff410113 100513 112423
  //   22400093 80e7 ff010113 112623 12023 100793 6500693 12703 f70733 e12023 178793 fef12823 fed12623
  //   fe812e23 fe912c23 30000413 ff014183 340233 100193 320023 fec14183 3401b3 18023 24183 ff114483 940233
  //   100493 920023 fed14483 9404b3 48023 24483 9181b3 ff214483 940233 100493 920023 fee14483 9404b3 48023
  //   24483 9181b3 ff314483 940233 100493 920023 fef14483 9404b3 48023 24483 9181b3 40000213 320233 24203
  //   ff812483 ffc12403 420233 420233 410233 1a400193 fe312823 bc00193 fe312623 fec22203 20067 12503
  //   fffff7b7 c4678793 f50533 fea12823 fe812e23 40800413 ff014183 3401b3 1c183 ff114203 440233 24203
  //   4181b3 ff214203 440233 24203 4181b3 ff314203 440233 24203 4181b3 40000213 320233 24503 ffc12403
  //   1400093 80e7 c12083 513 1010113 8067 22400213 20067 ff410113 48537 60050513 112423 a800093 80e7
  //   22400093 80e7 109*0 1 0 1010100 63*1010101 100 1000101 1010100 1000000 1010100 121*0 64*1000100
  //   64*2020000 64*3020100 0 4040404 0 4040404 0 4040404 0 4040404 0 4040404 0 4040404 0 4040404 0
  //   4040404 0 4040404 0 4040404 0 4040404 0 4040404 0 4040404 0 4040404 0 4040404 0 4040404 0 4040404 0
  //   4040404 0 4040404 0 4040404 0 4040404 0 4040404 0 4040404 0 4040404 0 4040404 0 4040404 0 4040404 0
  //   4040404 0 4040404 0 4040404 0 4040404 0 4040404 1000100 5040504 1000100 5040504 1000100 5040504
  //   1000100 5040504 1000100 5040504 1000100 5040504 1000100 5040504 1000100 5040504 1000100 5040504
  //   1000100 5040504 1000100 5040504 1000100 5040504 1000100 5040504 1000100 5040504 1000100 5040504
  //   1000100 5040504 1000100 5040504 1000100 5040504 1000100 5040504 1000100 5040504 1000100 5040504
  //   1000100 5040504 1000100 5040504 1000100 5040504 1000100 5040504 1000100 5040504 1000100 5040504
  //   1000100 5040504 1000100 5040504 1000100 5040504 1000100 5040504 1000100 5040504 2020000 6060404
  //   2020000 6060404 2020000 6060404 2020000 6060404 2020000 6060404 2020000 6060404 2020000 6060404
  //   2020000 6060404 2020000 6060404 2020000 6060404 2020000 6060404 2020000 6060404 2020000 6060404
  //   2020000 6060404 2020000 6060404 2020000 6060404 2020000 6060404 2020000 6060404 2020000 6060404
  //   2020000 6060404 2020000 6060404 2020000 6060404 2020000 6060404 2020000 6060404 2020000 6060404
  //   2020000 6060404 2020000 6060404 2020000 6060404 2020000 6060404 2020000 6060404 2020000 6060404
  //   2020000 6060404 3020100 7060504 3020100 7060504 3020100 7060504 3020100 7060504 3020100 7060504
  //   3020100 7060504 3020100 7060504 3020100 7060504 3020100 7060504 3020100 7060504 3020100 7060504
  //   3020100 7060504 3020100 7060504 3020100 7060504 3020100 7060504 3020100 7060504 3020100 7060504
  //   3020100 7060504 3020100 7060504 3020100 7060504 3020100 7060504 3020100 7060504 3020100 7060504
  //   3020100 7060504 3020100 7060504 3020100 7060504 3020100 7060504 3020100 7060504 3020100 7060504
  //   3020100 7060504 3020100 7060504 3020100 7060504 0 0 8080808 8080808 0 0 8080808 8080808 0 0 8080808
  //   8080808 0 0 8080808 8080808 0 0 8080808 8080808 0 0 8080808 8080808 0 0 8080808 8080808 0 0 8080808
  //   8080808 0 0 8080808 8080808 0 0 8080808 8080808 0 0 8080808 8080808 0 0 8080808 8080808 0 0 8080808
  //   8080808 0 0 8080808 8080808 0 0 8080808 8080808 0 0 8080808 8080808 1000100 1000100 9080908 9080908
  //   1000100 1000100 9080908 9080908 1000100 1000100 9080908 9080908 1000100 1000100 9080908 9080908
  //   1000100 1000100 9080908 9080908 1000100 1000100 9080908 9080908 1000100 1000100 9080908 9080908
  //   1000100 1000100 9080908 9080908 1000100 1000100 9080908 9080908 1000100 1000100 9080908 9080908
  //   1000100 1000100 9080908 9080908 1000100 1000100 9080908 9080908 1000100 1000100 9080908 9080908
  //   1000100 1000100 9080908 9080908 1000100 1000100 9080908 9080908 1000100 1000100 9080908 9080908
  //   2020000 2020000 a0a0808 a0a0808 2020000 2020000 a0a0808 a0a0808 2020000 2020000 a0a0808 a0a0808
  //   2020000 2020000 a0a080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
endmodule

module PC (
  input  [31:0] PC_in,
  input  PC_select,
  input  EN,
  input  clk,
  input  rst,
  output [31:0] PC_out
);

  wire [31:0] adder_1_out, multiplexer_1_out;

  Register #(.width(32)) register_1 (.D(multiplexer_1_out), .en(EN), .clk(clk), .Q(PC_out), .clr(rst));
  Multiplexer #(.width(32)) multiplexer_1 (.in0(adder_1_out), .in1(PC_in), .out(multiplexer_1_out), .sel(PC_select));
  Adder #(.width(32)) adder_1 (.a(PC_out), .b(32'h4), .out(adder_1_out));  // open: cin, cout

  // Notes on the sheet:
  //   add, addi, lui, lw, lbu, sw, sb, jalr
endmodule

module Fetch (
);
endmodule

module Controller (
  input  [6:0] opcode,
  input  [2:0] funct3,
  input  [6:0] funct7,
  output [1:0] ALUSelect,
  output pcSelect,
  output [2:0] instType,
  output wREN,
  output wMEN,
  output rMEN,
  output wordLS
);

  wire comparator_1_eq, comparator_2_eq, comparator_3_eq, comparator_4_eq, comparator_5_eq, comparator_6_eq,
       comparator_7_eq, comparator_8_eq, comparator_9_eq, nand_1_out, not_1_out, not_2_out, or_1_out,
       or_2_out, or_3_out;

  Comparator #(.width(5)) comparator_1 (.a(opcode[6:2]), .b(5'b01100), .eq(comparator_1_eq));  // open: gt, lt
  Comparator #(.width(5)) comparator_2 (.a(opcode[6:2]), .b(5'b00100), .eq(comparator_2_eq));  // open: gt, lt
  Comparator #(.width(5)) comparator_3 (.a(opcode[6:2]), .b({5{1'b0}}), .eq(comparator_3_eq));  // open: gt, lt
  Comparator #(.width(5)) comparator_4 (.a(opcode[6:2]), .b(5'b11001), .eq(comparator_4_eq));  // open: gt, lt
  Comparator #(.width(5)) comparator_5 (.a(opcode[6:2]), .b(5'b01000), .eq(comparator_5_eq));  // open: gt, lt
  Comparator #(.width(5)) comparator_6 (.a(opcode[6:2]), .b(5'b11000), .eq(comparator_6_eq));  // open: gt, lt
  Comparator #(.width(5)) comparator_7 (.a(opcode[6:2]), .b(5'b01101), .eq(comparator_7_eq));  // open: gt, lt
  Comparator #(.width(5)) comparator_8 (.a(opcode[6:2]), .b(5'b00101), .eq(comparator_8_eq));  // open: gt, lt
  Comparator #(.width(5)) comparator_9 (.a(opcode[6:2]), .b(5'b11101), .eq(comparator_9_eq));  // open: gt, lt
  nand nand_1 (nand_1_out, opcode[0], opcode[1]);
  or or_1 (or_1_out, comparator_2_eq, comparator_3_eq, comparator_4_eq);
  or or_2 (or_2_out, comparator_7_eq, comparator_8_eq);
  not not_1 (not_1_out, nand_1_out);
  not not_2 (not_2_out, nand_1_out);
  Comparator #(.width(3)) comparator_10 (.a(funct3), .b(3'b010), .eq(wordLS));  // open: gt, lt
  Priority_Encoder #(.select(2)) priority_encoder_1 (
    .in0(1'b1), .in1(comparator_1_eq), .in2(or_2_out), .out(ALUSelect));  // open: in3, gs, en_out, en_in
  and and_1 (pcSelect, comparator_9_eq, not_1_out);
  Priority_Encoder priority_encoder_2 (
    .in0(comparator_1_eq), .in1(or_1_out), .in2(comparator_5_eq), .in3(comparator_6_eq), .in4(or_2_out),
    .in5(comparator_9_eq), .in6(nand_1_out), .out(instType));  // open: in7, en_in, gs, en_out
  or or_3 (or_3_out, comparator_1_eq, or_1_out, comparator_6_eq, or_2_out, comparator_9_eq);
  and and_2 (wREN, or_3_out, not_2_out);
  and and_3 (wMEN, comparator_5_eq, not_2_out);
  and and_4 (rMEN, comparator_3_eq, not_2_out);
endmodule

module Registers (
  input  clk,
  input  rst,
  input  [3:0] rdR,
  input  [31:0] rdD,
  input  wEN,
  input  [3:0] rs1R,
  input  [3:0] rs2R,
  output [31:0] rs1D,
  output [31:0] rs2D
);

  wire and_1_out, and_2_out, and_3_out, and_4_out, and_5_out, and_6_out, and_7_out, and_8_out, and_9_out,
       and_10_out, and_11_out, and_12_out, and_13_out, and_14_out, and_15_out, decoder_1_out0,
       decoder_1_out1, decoder_1_out2, decoder_1_out3, decoder_2_out0, decoder_2_out1, decoder_2_out2,
       decoder_2_out3;
  wire [31:0] multiplexer_1_out, multiplexer_2_out, multiplexer_3_out, multiplexer_4_out, multiplexer_5_out,
       multiplexer_6_out, multiplexer_7_out, multiplexer_8_out, R1_q, R2_q, R3_q, R4_q, R5_q, R6_q, R7_q,
       R8_q, R9_q, R10_q, R11_q, R12_q, R13_q, R14_q, R15_q;

  Decoder #(.select(2)) decoder_1 (
    .out0(decoder_1_out0), .out1(decoder_1_out1), .out2(decoder_1_out2), .out3(decoder_1_out3),
    .sel(rdR[3:2]), .en(wEN));
  Decoder #(.select(2)) decoder_2 (
    .out0(decoder_2_out0), .out1(decoder_2_out1), .out2(decoder_2_out2), .out3(decoder_2_out3),
    .sel(rdR[1:0]), .en(wEN));
  and and_1 (and_1_out, decoder_2_out1, decoder_1_out0);
  and and_2 (and_2_out, decoder_2_out2, decoder_1_out0);
  and and_3 (and_3_out, decoder_2_out3, decoder_1_out0);
  Register #(.width(32)) R1 (.D(rdD), .en(and_1_out), .clk(clk), .Q(R1_q), .clr(rst));
  Register #(.width(32)) R2 (.D(rdD), .en(and_2_out), .clk(clk), .Q(R2_q), .clr(rst));
  Register #(.width(32)) R3 (.D(rdD), .en(and_3_out), .clk(clk), .Q(R3_q), .clr(rst));
  Register #(.width(32)) R4 (.D(rdD), .en(and_4_out), .clk(clk), .Q(R4_q), .clr(rst));
  and and_4 (and_4_out, decoder_2_out0, decoder_1_out1);
  Register #(.width(32)) R5 (.D(rdD), .en(and_5_out), .clk(clk), .Q(R5_q), .clr(rst));
  and and_5 (and_5_out, decoder_2_out1, decoder_1_out1);
  Register #(.width(32)) R6 (.D(rdD), .en(and_6_out), .clk(clk), .Q(R6_q), .clr(rst));
  and and_6 (and_6_out, decoder_2_out2, decoder_1_out1);
  Register #(.width(32)) R7 (.D(rdD), .en(and_7_out), .clk(clk), .Q(R7_q), .clr(rst));
  and and_7 (and_7_out, decoder_2_out3, decoder_1_out1);
  Register #(.width(32)) R8 (.D(rdD), .en(and_8_out), .clk(clk), .Q(R8_q), .clr(rst));
  and and_8 (and_8_out, decoder_2_out0, decoder_1_out2);
  Register #(.width(32)) R9 (.D(rdD), .en(and_9_out), .clk(clk), .Q(R9_q), .clr(rst));
  and and_9 (and_9_out, decoder_2_out1, decoder_1_out2);
  Register #(.width(32)) R10 (.D(rdD), .en(and_10_out), .clk(clk), .Q(R10_q), .clr(rst));
  and and_10 (and_10_out, decoder_2_out2, decoder_1_out2);
  Register #(.width(32)) R11 (.D(rdD), .en(and_11_out), .clk(clk), .Q(R11_q), .clr(rst));
  and and_11 (and_11_out, decoder_2_out3, decoder_1_out2);
  and and_12 (and_12_out, decoder_2_out0, decoder_1_out3);
  and and_13 (and_13_out, decoder_2_out1, decoder_1_out3);
  and and_14 (and_14_out, decoder_2_out2, decoder_1_out3);
  and and_15 (and_15_out, decoder_2_out3, decoder_1_out3);
  Register #(.width(32)) R12 (.D(rdD), .en(and_12_out), .clk(clk), .Q(R12_q), .clr(rst));
  Register #(.width(32)) R13 (.D(rdD), .en(and_13_out), .clk(clk), .Q(R13_q), .clr(rst));
  Register #(.width(32)) R14 (.D(rdD), .en(and_14_out), .clk(clk), .Q(R14_q), .clr(rst));
  Register #(.width(32)) R15 (.D(rdD), .en(and_15_out), .clk(clk), .Q(R15_q), .clr(rst));
  Multiplexer #(.select(2), .width(32)) multiplexer_1 (
    .in0({32{1'b0}}), .in1(R4_q), .in2(R8_q), .in3(R12_q), .out(multiplexer_1_out), .sel(rs1R[3:2]));
  Multiplexer #(.select(2), .width(32)) multiplexer_2 (
    .in0({32{1'b0}}), .in1(R4_q), .in2(R8_q), .in3(R12_q), .out(multiplexer_2_out), .sel(rs2R[3:2]));
  Multiplexer #(.select(2), .width(32)) multiplexer_3 (
    .in0(R1_q), .in1(R5_q), .in2(R9_q), .in3(R13_q), .out(multiplexer_3_out), .sel(rs1R[3:2]));
  Multiplexer #(.select(2), .width(32)) multiplexer_4 (
    .in0(R1_q), .in1(R5_q), .in2(R9_q), .in3(R13_q), .out(multiplexer_4_out), .sel(rs2R[3:2]));
  Multiplexer #(.select(2), .width(32)) multiplexer_5 (
    .in0(R2_q), .in1(R6_q), .in2(R10_q), .in3(R14_q), .out(multiplexer_5_out), .sel(rs1R[3:2]));
  Multiplexer #(.select(2), .width(32)) multiplexer_6 (
    .in0(R2_q), .in1(R6_q), .in2(R10_q), .in3(R14_q), .out(multiplexer_6_out), .sel(rs2R[3:2]));
  Multiplexer #(.select(2), .width(32)) multiplexer_7 (
    .in0(R3_q), .in1(R7_q), .in2(R11_q), .in3(R15_q), .out(multiplexer_7_out), .sel(rs1R[3:2]));
  Multiplexer #(.select(2), .width(32)) multiplexer_8 (
    .in0(R3_q), .in1(R7_q), .in2(R11_q), .in3(R15_q), .out(multiplexer_8_out), .sel(rs2R[3:2]));
  Multiplexer #(.select(2), .width(32)) multiplexer_9 (
    .in0(multiplexer_1_out), .in1(multiplexer_3_out), .in2(multiplexer_5_out), .in3(multiplexer_7_out),
    .out(rs1D), .sel(rs1R[1:0]));
  Multiplexer #(.select(2), .width(32)) multiplexer_10 (
    .in0(multiplexer_2_out), .in1(multiplexer_4_out), .in2(multiplexer_6_out), .in3(multiplexer_8_out),
    .out(rs2D), .sel(rs2R[1:0]));

  // Notes on the sheet:
  //   R0
endmodule

module Immediate (
  input  [2:0] instType,
  input  [31:0] instruction,
  output [31:0] imm
);

  wire [11:0] bit_extender_4_out;
  wire [19:0] bit_extender_3_out;
  wire [20:0] bit_extender_1_out, bit_extender_2_out;

  assign bit_extender_1_out = {{20{instruction[31]}}, instruction[31]};  // Bit_Extender bit_extender_1
  assign bit_extender_2_out = {{20{instruction[31]}}, instruction[31]};  // Bit_Extender bit_extender_2
  assign bit_extender_3_out = {{19{instruction[31]}}, instruction[31]};  // Bit_Extender bit_extender_3
  assign bit_extender_4_out = {{11{instruction[31]}}, instruction[31]};  // Bit_Extender bit_extender_4
  Multiplexer #(.select(3), .width(32)) multiplexer_1 (
    .in1({bit_extender_1_out, instruction[30:20]}),
    .in2({bit_extender_2_out, instruction[30:25], instruction[11:7]}),
    .in3({bit_extender_3_out, instruction[7], instruction[30:25], instruction[11:8], 1'b0}),
    .in4({instruction[31:12], {12{1'b0}}}),
    .in5({bit_extender_4_out, instruction[19:12], instruction[20], instruction[30:21], 1'b0}), .out(imm),
    .sel(instType));  // open: in0, in6, in7

  // Notes on the sheet:
  //   I_type
  //   S_type
  //   B_type
  //   U_type
  //   J_type
endmodule

module ALU (
  input  [1:0] ALUSelect,
  input  [31:0] A,
  input  [31:0] imm,
  input  [31:0] B,
  output [31:0] C
);

  wire [31:0] multiplexer_1_out, multiplexer_2_out;

  Multiplexer #(.width(32)) multiplexer_1 (.in0(A), .in1({32{1'b0}}), .out(multiplexer_1_out), .sel(ALUSelect[0]));
  Adder #(.width(32)) adder_1 (.a(multiplexer_1_out), .b(multiplexer_2_out), .out(C));  // open: cin, cout
  Multiplexer #(.width(32)) multiplexer_2 (.in0(imm), .in1(B), .out(multiplexer_2_out), .sel(ALUSelect[1]));
endmodule

module Memory (
  input  wordLS,
  input  [31:0] adress,
  input  [31:0] dataIn,
  input  [31:0] readIn,
  output byte3EN,
  output byte2EN,
  output byte1EN,
  output byte0EN,
  output [31:0] adressWord,
  output [31:0] writeOut,
  output [31:0] dataOut
);

  wire decoder_1_out0, decoder_1_out1, decoder_1_out2, decoder_1_out3;
  wire [7:0] multiplexer_1_out;
  wire [31:0] bit_extender_2_out;

  Multiplexer #(.select(2), .width(8)) multiplexer_1 (
    .in0(readIn[7:0]), .in1(readIn[15:8]), .in2(readIn[23:16]), .in3(readIn[31:24]), .out(multiplexer_1_out),
    .sel(adress[1:0]));
  assign adressWord = {{2{1'b0}}, adress[31:2]};  // Bit_Extender bit_extender_1
  assign bit_extender_2_out = {{24{1'b0}}, multiplexer_1_out};  // Bit_Extender bit_extender_2
  Decoder #(.select(2)) decoder_1 (
    .out0(decoder_1_out0), .out1(decoder_1_out1), .out2(decoder_1_out2), .out3(decoder_1_out3),
    .sel(adress[1:0]));  // open: en
  Multiplexer #(.width(32)) multiplexer_2 (.in0(bit_extender_2_out), .in1(readIn), .out(dataOut), .sel(wordLS));
  or or_1 (byte3EN, wordLS, decoder_1_out0);
  or or_2 (byte2EN, wordLS, decoder_1_out1);
  or or_3 (byte1EN, wordLS, decoder_1_out2);
  or or_4 (byte0EN, wordLS, decoder_1_out3);

  assign writeOut = dataIn;
endmodule
