// Logisim project F3.circ as structural Verilog: 2 circuits, main circuit main
module main (
  input  \或门 ,
  input  in_2,
  input  \异或门 ,
  input  in_4,
  input  \同或门 ,
  input  in_6,
  input  \_2_4译码器 ,
  input  in_8
);

  wire and_1_out, and_2_out, and_3_out, and_4_out, and_5_out, and_6_out, nor_1_out, nor_2_out, nor_3_out,
       not_1_out, not_2_out, or_1_out, transistor_1_out, transistor_2_out, transistor_5_out;

  not not_1 (not_1_out, \_2_4译码器 );
  Transistor #(.\type ("n")) transistor_1 (.in(1'b0), .out(transistor_1_out), .gate(\或门 ));
  and and_1 (and_1_out, \异或门 , in_4);
  and and_2 (and_2_out, \同或门 , in_6);
  not not_2 (not_2_out, in_8);
  and and_3 (and_3_out, \_2_4译码器 , in_8);
  // Probe on and_3_out
  Transistor transistor_2 (.in(1'b1), .out(transistor_2_out), .gate(\或门 ));
  Transistor transistor_3 (.in(transistor_2_out), .out(transistor_1_out), .gate(in_2));
  Transistor #(.\type ("n")) transistor_4 (.in(1'b0), .out(transistor_1_out), .gate(in_2));
  nor nor_1 (nor_1_out, \异或门 , in_4);
  nor nor_2 (nor_2_out, \同或门 , in_6);
  and and_4 (and_4_out, \_2_4译码器 , not_2_out);
  // Probe on and_4_out
  Transistor transistor_5 (.in(1'b1), .out(transistor_5_out), .gate(transistor_1_out));
  LED led_1 (.in(transistor_5_out));
  Transistor #(.\type ("n")) transistor_6 (.in(1'b0), .out(transistor_5_out), .gate(transistor_1_out));
  nor nor_3 (nor_3_out, and_1_out, nor_1_out);
  LED led_2 (.in(nor_3_out));
  or or_1 (or_1_out, and_2_out, nor_2_out);
  LED led_3 (.in(or_1_out));
  and and_5 (and_5_out, not_1_out, in_8);
  // Probe on and_5_out
  // Probe on and_6_out
  and and_6 (and_6_out, not_1_out, not_2_out);
endmodule

module decoder2to4 (
  input  in0,
  input  in1,
  output out1,
  output out2,
  output out3,
  output out4
);

  wire not_1_out, not_2_out;

  not not_1 (not_1_out, in1);
  not not_2 (not_2_out, in0);
  and and_1 (out4, in1, in0);
  and and_2 (out3, in1, not_2_out);
  and and_3 (out2, not_1_out, in0);
  and and_4 (out1, not_1_out, not_2_out);
endmodule
